# Fritzing sketch pi-attiny85-433mhz 2 (saved by Fritzing 0.8.3b)
breadboards: 1

parts:
  U1 = attiny85 [package=dip]
  BB1 = 4-Line Bi-Directional Level Shifter
  Pi1 = Adafruit Pi Cobbler
  R1 = Resistor [tolerance=±5% resistance=220 package=THT]
  LED1 = LED - 3mm [color="Red (633nm)" package="3 mm [THT]"]
  R2 = Resistor [tolerance=±5% resistance=10k package=THT]

nets:
  N1: U1.Pin_1, R2.Pin_1
  N2: U1.Pin_4, BB1.GND#6, Pi1.GND, R1.Pin_0
  N3: U1.Pin_5, BB1.B1
  N4: U1.Pin_6, LED1.anode
  N5: U1.Pin_7, BB1.B2
  N6: U1.Pin_8, BB1.HV, Pi1.5V0, R2.Pin_0
  N7: BB1.LV, Pi1.3V3
  N8: BB1.A1, Pi1.SDA0
  N9: BB1.A2, Pi1.SCL0
  N10: R1.Pin_1, LED1.cathode

notes:
  433Mhz power
  433 signal
  433 Ground

custom parts:
  4-Line Bi-Directional Level Shifter: 4-Channel Bi-Directional Level Shifter
  Adafruit Pi Cobbler: Adafruit Pi Cobbler GPIO Breakout for Raspberry Pi
