# Fritzing sketch Tripple sensor using I2C (saved by Fritzing 0.9.0b)
breadboards: 1

parts:
  Onderdeel1 = Arduino Uno (Rev3)
  LED3 = LED - 3mm [color="Yellow (595nm)" package="3 mm [THT]"]
  LED2 = LED - 3mm [color="Red (633nm)" package="3 mm [THT]"]
  LED1 = LED - 3mm [color="Green (570nm)" package="3 mm [THT]"]
  R1 = Resistor [tolerance=±5% resistance=220 package=THT]
  R2 = Resistor [tolerance=±5% resistance=220 package=THT]
  R3 = Resistor [tolerance=±5% resistance=220 package=THT]
  R4 = Resistor [tolerance=±5% resistance=220 package=THT]
  R5 = Resistor [tolerance=±5% resistance=220 package=THT]
  R6 = Resistor [tolerance=±5% resistance=220 package=THT]
  U1 = QRD1114 [package=qrd1114]
  U2 = QRD1114 [package=qrd1114]
  U3 = QRD1114 [package=qrd1114]
  IC1 = Dual Bidirectional Bus Buffer - P82B96P [part_number=P82B96P package="DIP (Dual Inline) [THT]"]
  R7 = Resistor [tolerance=±5% resistance=220 package=THT]
  R8 = Resistor [tolerance=±5% resistance=220 package=THT]
  R9 = Resistor [tolerance=±5% resistance=220 package=THT]
  R10 = Resistor [tolerance=±5% resistance=330 package=THT]
  R11 = Resistor [tolerance=±5% resistance=330 package=THT]
  C1 = Electrolytic Capacitor [capacitance=10µF voltage=20V package="100 mil [THT, electrolytic]"]
  J1 = Screw terminal - 2 pins [package=THT]

nets:
  N1: Onderdeel1.A0, U1.E, R8.Pin_0
  N2: Onderdeel1.A1, U2.E, R9.Pin_0
  N3: Onderdeel1.A2, U3.E, R7.Pin_0
  N4: Onderdeel1.A4/SDA, IC1.Sy
  N5: Onderdeel1.A5/SCL, IC1.Sx
  GND: Onderdeel1.GND, LED3.anode, LED2.anode, LED1.anode, U1.K, U2.K, IC1.GND, R8.Pin_1, R9.Pin_1, C1.-
  N6: Onderdeel1.D0/RX, R3.Pin_0
  N7: Onderdeel1.D1/TX, R1.Pin_0
  N8: Onderdeel1.D2, R2.Pin_0
  5V: Onderdeel1.5V, R4.Pin_1, R5.Pin_1, R6.Pin_1, U1.C, U2.C, U3.C, IC1.Vcc, R10.Pin_0, R11.Pin_0, C1.+
  N9: LED3.cathode, R1.Pin_1
  N10: LED2.cathode, R2.Pin_1
  N11: LED1.cathode, R3.Pin_1
  N12: R4.Pin_0, U1.A
  N13: R5.Pin_0, U2.A
  N14: R6.Pin_0, U3.A
  N15: U3.K, R7.Pin_1
  N16: IC1.Rx, IC1.Tx, R10.Pin_1, J1.pin2
  N17: IC1.Ty, IC1.Ry, R11.Pin_1, J1.pin1

notes:
  I2C SCL
  I2C SDA
