# Fritzing sketch PiDome I2C-LTS-LC (saved by Fritzing 0.8.3b)
breadboards: 1

parts:
  Onderdeel1 = Arduino Uno (Rev3)
  U1 = Voltage Regulator - 5V [package="TO220 [THT]"]
  U2 = Voltage Regulator - 5V [package="TO220 [THT]"]
  C1 = Electrolytic Capacitor [capacitance=1µF voltage=50V package="100 mil [THT, electrolytic]"]
  R1 = Photocell (LDR) [package=THT]
  T1 = TMP36 Temperature Sensor [package="TO92 [THT]"]
  Raspberry_Pi_rev1 = Raspberry Pi rev2
  R2 = Resistor [tolerance=±5% resistance=1k package=THT]
  J2 = screw terminal, 2 pins  # not connected
  R3 = Resistor [tolerance=±5% resistance=1k package=THT]
  R4 = Resistor [tolerance=±5% resistance=1k package=THT]
  LED1 = LED - 3mm [color="Red (633nm)" package="3 mm [THT]"]
  D6 = Rectifier Diode [part_number=1N4001 package="300 mil [THT]"]
  D7 = Rectifier Diode [part_number=1N4001 package="300 mil [THT]"]
  R5 = Resistor [tolerance=±5% resistance=1.5k package=THT]
  D8 = Rectifier Diode [part_number=1N4001 package="300 mil [THT]"]
  NeoPixel_Digital_RGB_LED_Strip1 = Adafruit NeoPixel Digital RGB LED Strip
  NeoPixel_Digital_RGB_LED_Strip2 = Adafruit NeoPixel Digital RGB LED Strip
  NeoPixel_Digital_RGB_LED_Strip3 = Adafruit NeoPixel Digital RGB LED Strip
  D9 = Rectifier Diode [part_number=1N4001 package="300 mil [THT]"]
  D10 = Rectifier Diode [part_number=1N4001 package="300 mil [THT]"]
  D11 = Rectifier Diode [part_number=1N4001 package="300 mil [THT]"]
  D12 = Rectifier Diode [part_number=1N4001 package="300 mil [THT]"]
  D13 = Rectifier Diode [part_number=1N4001 package="300 mil [THT]"]

nets:
  N1: Onderdeel1.A0, T1.Vout
  N2: Onderdeel1.A1, R1.pin_0, R5.Pin_0
  N3: Onderdeel1.A4/SDA, Raspberry_Pi_rev1.GIPO_2, R4.Pin_0
  N4: Onderdeel1.A5/SCL, Raspberry_Pi_rev1.GIPO_3, R3.Pin_0
  GND: Onderdeel1.GND, U1.GND, U2.GND, C1.-, T1.GND, Raspberry_Pi_rev1.GND, R2.Pin_1, R5.Pin_1, D8.cathode
  N5: Onderdeel1.AREF, U1.output_voltage, C1.+, R1.pin_1, T1.+Vs, R3.Pin_1, R4.Pin_1, LED1.anode
  N6: Onderdeel1.D3_PWM, NeoPixel_Digital_RGB_LED_Strip1.DIN
  N7: U1.input_voltage, D6.cathode
  N8: U2.input_voltage, D7.cathode
  +5V: U2.output_voltage, NeoPixel_Digital_RGB_LED_Strip1.+5V, NeoPixel_Digital_RGB_LED_Strip2.+5V, NeoPixel_Digital_RGB_LED_Strip3.+5V
  N9: R2.Pin_0, LED1.cathode
  N10: D6.anode, D7.anode, D13.cathode
  GND_2: D8.anode, NeoPixel_Digital_RGB_LED_Strip1.GND, NeoPixel_Digital_RGB_LED_Strip2.GND, NeoPixel_Digital_RGB_LED_Strip3.GND
  N11: NeoPixel_Digital_RGB_LED_Strip1.DO, NeoPixel_Digital_RGB_LED_Strip2.DIN
  N12: NeoPixel_Digital_RGB_LED_Strip2.DO, NeoPixel_Digital_RGB_LED_Strip3.DIN
  N13: D9.cathode, D10.anode
  N14: D9.anode, D11.cathode
  N15: D10.cathode, D12.anode
  N16: D12.cathode, D13.anode

custom parts:
  Adafruit NeoPixel Digital RGB LED Strip: Digitally addressable NeoPixel RGB LED strip by Adafruit Industries
  Adafruit NeoPixel Digital RGB LED Strip: Digitally addressable NeoPixel RGB LED strip from Adafruit Industries
