# Fritzing sketch PiDome IR Tranceiver - Fritzing (saved by Fritzing 0.9.0b)
breadboards: 1

parts:
  Onderdeel1 = Arduino Uno (Rev3)
  R1 = Resistor [tolerance=±5% resistance=220 package=THT]
  R2 = Resistor [tolerance=±5% resistance=220 package=THT]
  LED1 = LED - 3mm [color="Blue (430nm)" package="3 mm [THT]"]
  LED2 = LED - 3mm [color="Red (633nm)" package="3 mm [THT]"]
  LED3 = LED - 3mm [color="Green (555nm)" package="3 mm [THT]"]
  R3 = Resistor [tolerance=±5% resistance=220 package=THT]
  Q1 = NPN-Transistor [part_number=BC547 package="TO92 [THT]"]
  R4 = Resistor [tolerance=±5% resistance=47 package=THT]
  LED4 = LED - 5mm [color="Infrared (940nm)" package="5 mm [THT]"]
  R5 = Resistor [tolerance=±5% resistance=4.7k package=THT]
  C1 = Ceramic Capacitor [capacitance=10µF part_number=104 package="100 mil [THT, multilayer]"]
  S1 = Pushbutton [package="[THT]"]
  S2 = Pushbutton [package="[THT]"]
  S3 = Pushbutton [package="[THT]"]
  C2 = Electrolytic Capacitor [capacitance=100µF package="100 mil [THT, electrolytic]"]
  R6 = Resistor [tolerance=±5% resistance=1k package=THT]
  R7 = Resistor [tolerance=±5% resistance=1k package=THT]
  R8 = Resistor [tolerance=±5% resistance=1k package=THT]
  IR1 = TSOP312.., 314.. [package=THT]

nets:
  N1: Onderdeel1.D11_PWM/MOSI, IR1.Data
  N2: Onderdeel1.D13/SCK, R3.Pin_0
  GND: Onderdeel1.GND, LED1.cathode, LED2.cathode, LED3.cathode, Q1.C, C1.0, C2.-, R6.Pin_0, R7.Pin_0, R8.Pin_0, IR1.GND
  N3: Onderdeel1.D2, R1.Pin_0
  N4: Onderdeel1.D3_PWM, R5.Pin_1
  N5: Onderdeel1.D4, R2.Pin_0
  N6: Onderdeel1.D5_PWM, S1.Pin_3, S1.Pin_4, R6.Pin_1
  N7: Onderdeel1.D6_PWM, S2.Pin_3, S2.Pin_4, R7.Pin_1
  N8: Onderdeel1.D7, S3.Pin_3, S3.Pin_4, R8.Pin_1
  N9: Onderdeel1.5V, LED4.anode, C1.1, S1.Pin_1, S1.Pin_2, S2.Pin_1, S2.Pin_2, S3.Pin_1, S3.Pin_2, C2.+, IR1.Vs
  N10: R1.Pin_1, LED1.anode
  N11: R2.Pin_1, LED2.anode
  N12: LED3.anode, R3.Pin_1
  N13: Q1.E, R4.Pin_1
  N14: Q1.B, R5.Pin_0
  N15: R4.Pin_0, LED4.cathode

notes:
  Be sure to select the appropiate resistor values attached to your IR led
  Some IR transmitter LED's can be driven up to 500 milliamps. Refer to the IR led specifications. The higher the better the range, BUT:
  If this is the case it for your IR LED it would be handy not to feed the IR led from the Arduino board.
  The schematic shows a lower amount of milliamps used.
