# Fritzing sketch Raspberry Pi GPIO Relay-switch (saved by Fritzing 0.9.0b)
breadboards: 1

parts:
  Pi1 = Adafruit Pi Cobbler
  U2 = RELAY [package=relay-g5q]
  R1 = Resistor [tolerance=±5% resistance=220 package=THT]
  LED1 = LED - 5mm [color="Red (633nm)" package="5 mm [THT]"]
  D1 = Rectifier Diode [part_number=1N4001 package="300 mil [THT]"]
  D2 = Rectifier Diode [part_number=1N4001 package="300 mil [THT]"]
  R2 = Resistor [tolerance=±5% resistance=220 package=THT]
  Q2 = NPN-Transistor [package="TO92 [THT]"]

nets:
  N1: Pi1.GND, R1.Pin_1, Q2.C
  N2: Pi1.#25, LED1.anode, R2.Pin_0
  N3: U2.COIL2, D1.anode, Q2.E
  N4: U2.COIL1, D1.cathode
  N5: R1.Pin_0, LED1.cathode
  N6: D2.cathode, Q2.B
  N7: D2.anode, R2.Pin_1

notes:
  LOAD
  12Vcc (make  sure ground is shared too)
  WARNING: As it is possible to switch mains, it's not adviced without optocouplers or other security!

custom parts:
  Adafruit Pi Cobbler: Adafruit Pi Cobbler GPIO Breakout for Raspberry Pi
